# Fritzing sketch ESP01_NowSender (saved by Fritzing 0.9.4)
breadboards: 1

parts:
  U1 = ESP8266 ESP-01 Upgraded WiFi Module [part_number=ESP8266]
  DHT1 = DHT22 Humidity and Temperature Sensor
  R2 = Resistor [tolerance=±5% power=0.25 resistance=10k package=THT]
  VCC1 = Battery block 9V
  M2 = RioRand LM2596
  R1 = Resistor [tolerance=±5% resistance=10k power=0.25 package=THT]

nets:
  VCC: U1.VCC, DHT1.VDD, R2.Pin_0, M2.Pin_3, R1.Pin_0
  N1: U1.GPIO_0, DHT1.DATA, R2.Pin_1
  N2: U1.CH_PD, R1.Pin_1
  GND: U1.GND, DHT1.GND, M2.Pin_4
  N3: VCC1.-, M2.Pin_2
  N4: VCC1.+, M2.Pin_1

custom parts:
  ESP8266 ESP-01 Upgraded WiFi Module: Upgraded Version ESP-01,all Flash are upgraded to 1M byte.Also support Cloud service remote transmission.
